// Logisim project Circuito de 4 entardas e 1 saida.circ as structural Verilog: 2 circuits, main circuit Circuito de 4 entradas e 1 saida 2
module Circuito_de_4_entradas_e_1_saida_2 (
  input  A,
  input  B,
  input  C,
  input  D,
  output S
);

  wire and_1_out, and_2_out, and_3_out, and_4_out, not_1_out, not_2_out, not_3_out, or_1_out;

  not not_1 (not_1_out, C);
  not not_2 (not_2_out, D);
  not not_3 (not_3_out, B);
  and and_1 (and_1_out, not_3_out, C);
  and and_2 (and_2_out, A, not_1_out);
  and and_3 (and_3_out, A, not_2_out);
  and and_4 (and_4_out, not_2_out, and_1_out);
  or or_1 (or_1_out, and_2_out, and_3_out);
  or or_2 (S, or_1_out, and_4_out);
endmodule

module main (
  input  in_1,
  input  in_2,
  input  in_3,
  input  in_4,
  output out_5
);

  Circuito_de_4_entradas_e_1_saida_2 circuito_de_4_entradas_e_1_saida_2_1 (
    .S(out_5), .A(in_1), .B(in_2), .C(in_3), .D(in_4));
endmodule
